// Logisim project CH016M01.circ as structural Verilog: 11 circuits, main circuit CH016M01
module CH016M01 (
  input  INT,
  input  [15:0] FROM_RAM,
  input  resume,
  input  CLR,
  output STEP_1,
  output [15:0] TO_RAM,
  output RAM_WE,
  output RAM_RE,
  output [15:0] TO_ADDR
);

  wire control_unit_1_alu_abs, control_unit_1_alu_add, control_unit_1_alu_and, control_unit_1_alu_carry,
       control_unit_1_alu_i_flags, control_unit_1_alu_inc, control_unit_1_alu_neg, control_unit_1_alu_not,
       control_unit_1_alu_or, control_unit_1_alu_rotate, control_unit_1_alu_shift,
       control_unit_1_alu_shift_a, control_unit_1_alu_shift_left, control_unit_1_alu_sub,
       control_unit_1_alu_x_passthrough, control_unit_1_alu_xor, control_unit_1_alu_y_embeded,
       control_unit_1_flags_load, control_unit_1_flags_load_bus, control_unit_1_flags_re,
       control_unit_1_flags_we, control_unit_1_gpr_re, control_unit_1_gpr_we, control_unit_1_imm_we,
       control_unit_1_int_disable, control_unit_1_int_enable, control_unit_1_iss_we, control_unit_1_pc_load,
       control_unit_1_pc_re, control_unit_1_pc_we, control_unit_1_sp_dec, control_unit_1_sp_inc,
       interrupt_service_system_1_int_out;
  wire [1:0] arithmetic_logic_unit_1_flags_write, control_unit_1_gpr_addr_mode, control_unit_1_ram_addr_mode,
       control_unit_1_ram_addr_mode_2, flags_register_1_alu_in;
  wire [3:0] control_unit_1_x_op, control_unit_1_y_op;
  wire [15:0] adder_1_out, arithmetic_logic_unit_1_result, bit_extender_1_out, flags_register_1_data_out,
       immediate_register_1_data_out, interrupt_service_system_1_data_out, multiplexer_1_out,
       multiplexer_2_out, multiplexer_4_out, multiplexer_5_out, or_1_out, program_counter_1_addr_out,
       program_counter_1_data_out, register_file_1_data_out, register_file_1_x_out, register_file_1_y_out;

  Control_Unit control_unit_1 (
    .FLAGS_WE(control_unit_1_flags_we), .FLAGS_LOAD(control_unit_1_flags_load),
    .FLAGS_LOAD_BUS(control_unit_1_flags_load_bus), .IMM_WE(control_unit_1_imm_we),
    .FLAGS_RE(control_unit_1_flags_re), .Y_OP(control_unit_1_y_op), .ALU_ADD(control_unit_1_alu_add),
    .ALU_CARRY(control_unit_1_alu_carry), .ALU_SUB(control_unit_1_alu_sub), .ALU_INC(control_unit_1_alu_inc),
    .ALU_ABS(control_unit_1_alu_abs), .ALU_NEG(control_unit_1_alu_neg),
    .ALU_I_FLAGS(control_unit_1_alu_i_flags), .ALU_SHIFT(control_unit_1_alu_shift),
    .ALU_SHIFT_LEFT(control_unit_1_alu_shift_left), .ALU_SHIFT_A(control_unit_1_alu_shift_a),
    .ALU_ROTATE(control_unit_1_alu_rotate), .ALU_Y_EMBEDED(control_unit_1_alu_y_embeded),
    .ALU_AND(control_unit_1_alu_and), .ALU_OR(control_unit_1_alu_or), .ALU_XOR(control_unit_1_alu_xor),
    .ALU_NOT(control_unit_1_alu_not), .ALU_X_PASSTHROUGH(control_unit_1_alu_x_passthrough),
    .PC_LOAD(control_unit_1_pc_load), .RAM_RE(RAM_RE), .PC_WE(control_unit_1_pc_we),
    .GPR_WE(control_unit_1_gpr_we), .RAM_ADDR_MODE(control_unit_1_ram_addr_mode), .RAM_WE(RAM_WE),
    .GPR_RE(control_unit_1_gpr_re), .SP_INC(control_unit_1_sp_inc), .SP_DEC(control_unit_1_sp_dec),
    .RAM_ADDR_MODE_2(control_unit_1_ram_addr_mode_2), .GPR_ADDR_MODE(control_unit_1_gpr_addr_mode),
    .PC_RE(control_unit_1_pc_re), .INT_DISABLE(control_unit_1_int_disable),
    .INT_ENABLE(control_unit_1_int_enable), .ISS_WE(control_unit_1_iss_we), .X_OP(control_unit_1_x_op),
    .STEP(STEP_1), .INSTRUCTION(FROM_RAM), .CLR(CLR), .RESUME(resume),
    .EXT_INT(interrupt_service_system_1_int_out), .FLAGS_IN(flags_register_1_alu_in));
  assign bit_extender_1_out = {{12{1'b0}}, control_unit_1_y_op};  // Bit_Extender bit_extender_1
  Multiplexer #(.enable("false"), .width(16)) multiplexer_1 (
    .in0(register_file_1_y_out), .in1(bit_extender_1_out), .out(multiplexer_1_out),
    .sel(control_unit_1_alu_y_embeded));
  Multiplexer #(.enable("false"), .select(2), .width(16)) multiplexer_2 (
    .in0(FROM_RAM), .in1(immediate_register_1_data_out), .in2(register_file_1_x_out),
    .in3(interrupt_service_system_1_data_out), .out(multiplexer_2_out), .sel(control_unit_1_ram_addr_mode_2));
  Adder #(.width(16)) adder_1 (
    .a(register_file_1_y_out), .b(immediate_register_1_data_out), .out(adder_1_out));  // open: cin, cout
  Multiplexer #(.enable("false"), .select(2), .width(16)) multiplexer_3 (
    .in0(program_counter_1_addr_out), .in1(immediate_register_1_data_out), .in2(register_file_1_y_out),
    .in3(adder_1_out), .out(TO_ADDR), .sel(control_unit_1_ram_addr_mode));
  Program_Counter program_counter_1 (
    .ADDR_OUT(program_counter_1_addr_out), .DATA_OUT(program_counter_1_data_out),
    .DATA_IN(multiplexer_2_out), .LOAD(control_unit_1_pc_load), .WE(control_unit_1_pc_we), .CLR(CLR),
    .RE(control_unit_1_pc_re));
  Interrupt_Service_System interrupt_service_system_1 (
    .DATA_OUT(interrupt_service_system_1_data_out), .INT_OUT(interrupt_service_system_1_int_out),
    .ENABLE(control_unit_1_int_enable), .DISABLE(control_unit_1_int_disable), .WE(control_unit_1_iss_we),
    .INT_IN(INT), .CLR(CLR), .DATA_IN(FROM_RAM));
  Register_File register_file_1 (
    .DATA_OUT(register_file_1_data_out), .Y_OUT(register_file_1_y_out), .X_OUT(register_file_1_x_out),
    .DATA_IN(multiplexer_4_out), .WE(control_unit_1_gpr_we), .XOP(control_unit_1_x_op),
    .YOP(control_unit_1_y_op), .SP_INC(control_unit_1_sp_inc), .SP_DEC(control_unit_1_sp_dec), .CLR(CLR),
    .RE(control_unit_1_gpr_re));
  Arithmetic_Logic_Unit arithmetic_logic_unit_1 (
    .FLAGS_WRITE(arithmetic_logic_unit_1_flags_write), .RESULT(arithmetic_logic_unit_1_result),
    .NEG(control_unit_1_alu_abs), .ABS(control_unit_1_alu_neg), .INC(control_unit_1_alu_inc),
    .A_OPERAND(register_file_1_x_out), .B_OPERAND(multiplexer_1_out), .FLAGS_READ(flags_register_1_alu_in),
    .I_FLAGS(control_unit_1_alu_i_flags), .ADD(control_unit_1_alu_add), .SHIFT(control_unit_1_alu_shift),
    .LEFT(control_unit_1_alu_shift_left), .CARRY(control_unit_1_alu_carry),
    .ROTATE(control_unit_1_alu_rotate), .A_SHIFT(control_unit_1_alu_shift_a), .SUB(control_unit_1_alu_sub),
    .AND(control_unit_1_alu_and), .OR(control_unit_1_alu_or), .XOR(control_unit_1_alu_xor),
    .NOT(control_unit_1_alu_not), .X_PASS_THROUGH(control_unit_1_alu_x_passthrough));
  Flags_Register flags_register_1 (
    .ALU_IN(flags_register_1_alu_in), .DATA_OUT(flags_register_1_data_out),
    .ALU_OUT(arithmetic_logic_unit_1_flags_write), .DATA_IN(multiplexer_5_out),
    .LOAD(control_unit_1_flags_load), .WE(control_unit_1_flags_we), .CLR(CLR), .RE(control_unit_1_flags_re));
  Immediate_Register immediate_register_1 (
    .DATA_OUT(immediate_register_1_data_out), .DATA_IN(FROM_RAM), .WE(control_unit_1_imm_we), .CLR(CLR));
  Multiplexer #(.enable("false"), .select(2), .width(16)) multiplexer_4 (
    .in0(FROM_RAM), .in1(flags_register_1_data_out), .in2(arithmetic_logic_unit_1_result),
    .in3(register_file_1_y_out), .out(multiplexer_4_out), .sel(control_unit_1_gpr_addr_mode));
  Multiplexer #(.enable("false"), .width(16)) multiplexer_5 (
    .in0(register_file_1_x_out), .in1(FROM_RAM), .out(multiplexer_5_out), .sel(control_unit_1_flags_load_bus));
  assign or_1_out = program_counter_1_data_out | register_file_1_data_out | flags_register_1_data_out;  // OR_Gate or_1, 16 bits wide
  assign TO_RAM = RAM_WE ? or_1_out : 16'bz;  // Controlled_Buffer controlled_buffer_1
endmodule

module Instruction_Register (
  input  [15:0] DATA_IN,
  input  WE,
  input  CLR,
  output [4:0] ALU_OPERATION,
  output [7:0] INSTRUCTION_OUT,
  output [3:0] X_OPERAND,
  output [3:0] Y_OPERAND
);

  wire clock_1_out;

  Register #(.width(16)) Instruction (
    .D(DATA_IN), .en(WE), .clk(clock_1_out), .Q({INSTRUCTION_OUT[7:5], ALU_OPERATION, Y_OPERAND, X_OPERAND}),
    .clr(CLR));
  Clock clock_1 (.out(clock_1_out));

  assign INSTRUCTION_OUT[4:0] = ALU_OPERATION;
endmodule

module Control_Unit (
  input  EXT_INT,
  input  [15:0] INSTRUCTION,
  input  CLR,
  input  RESUME,
  input  [1:0] FLAGS_IN,
  output [3:0] X_OP,
  output STEP,
  output IMM_WE,
  output INT_DISABLE,
  output INT_ENABLE,
  output ISS_WE,
  output FLAGS_RE,
  output FLAGS_WE,
  output RAM_RE,
  output FLAGS_LOAD,
  output FLAGS_LOAD_BUS,
  output RAM_WE,
  output ALU_ADD,
  output ALU_CARRY,
  output ALU_SUB,
  output [1:0] RAM_ADDR_MODE,
  output ALU_INC,
  output ALU_ABS,
  output ALU_NEG,
  output ALU_I_FLAGS,
  output ALU_SHIFT,
  output ALU_SHIFT_LEFT,
  output ALU_SHIFT_A,
  output ALU_ROTATE,
  output ALU_Y_EMBEDED,
  output ALU_AND,
  output ALU_OR,
  output ALU_XOR,
  output ALU_NOT,
  output ALU_X_PASSTHROUGH,
  output PC_RE,
  output [3:0] Y_OP,
  output PC_WE,
  output PC_LOAD,
  output [1:0] RAM_ADDR_MODE_2,
  output GPR_RE,
  output GPR_WE,
  output SP_INC,
  output SP_DEC,
  output [1:0] GPR_ADDR_MODE
);

  wire and_1_out, and_2_out, and_3_out, and_4_out, and_5_out, and_6_out, and_7_out, and_8_out, and_9_out,
       and_10_out, and_11_out, and_12_out, and_13_out, and_14_out, and_15_out, and_16_out, and_17_out,
       and_19_out, and_20_out, and_21_out, and_22_out, and_23_out, and_24_out, and_25_out, and_26_out,
       and_27_out, and_28_out, and_29_out, and_30_out, and_31_out, and_32_out, and_33_out, and_34_out,
       and_35_out, and_36_out, and_37_out, and_38_out, and_39_out, and_40_out, and_41_out, and_42_out,
       and_43_out, and_44_out, and_45_out, and_46_out, and_47_out, and_48_out, and_49_out, and_50_out,
       and_51_out, and_52_out, and_53_out, demultiplexer_1_out0, demultiplexer_1_out1, demultiplexer_1_out2,
       demultiplexer_1_out4, demultiplexer_1_out5, demultiplexer_1_out6, demultiplexer_1_out8,
       demultiplexer_1_out9, demultiplexer_1_out10, demultiplexer_1_out11, demultiplexer_1_out12,
       demultiplexer_1_out13, demultiplexer_1_out14, demultiplexer_1_out15, demultiplexer_1_out16,
       demultiplexer_1_out17, demultiplexer_1_out18, demultiplexer_1_out19, demultiplexer_1_out20,
       demultiplexer_1_out24, demultiplexer_1_out26, instruction_decoder_1_alu_operation,
       instruction_decoder_1_brk, instruction_decoder_1_call_direct, instruction_decoder_1_call_indirect,
       instruction_decoder_1_hlt, instruction_decoder_1_int_call, instruction_decoder_1_int_disable,
       instruction_decoder_1_int_enable, instruction_decoder_1_isr, instruction_decoder_1_jmp_direct,
       instruction_decoder_1_jmp_indirect, instruction_decoder_1_ld, instruction_decoder_1_ld_imm,
       instruction_decoder_1_ld_st_imm_ptr, instruction_decoder_1_ld_st_indirect,
       instruction_decoder_1_ld_st_indirect_offset, instruction_decoder_1_mov_flags_reg,
       instruction_decoder_1_mov_reg_flags, instruction_decoder_1_mov_reg_reg,
       instruction_decoder_1_pop_flags, instruction_decoder_1_pop_reg, instruction_decoder_1_push_flags,
       instruction_decoder_1_push_reg, instruction_decoder_1_ret, instruction_decoder_1_rti,
       instruction_decoder_1_st, nand_1_out, not_1_out, not_2_out, not_3_out, not_4_out, not_5_out,
       not_6_out, not_7_out, or_2_out, or_6_out, or_7_out, or_10_out, or_11_out, or_12_out, or_13_out,
       or_14_out, or_15_out, or_16_out, or_17_out, or_18_out, or_19_out, or_20_out, or_25_out, or_26_out,
       or_27_out, or_28_out, or_29_out, or_30_out, or_31_out, or_32_out, or_33_out, or_34_out, or_35_out,
       or_38_out, or_42_out, or_43_out, or_44_out, or_45_out, or_48_out, or_49_out, or_54_out, or_55_out,
       or_56_out, or_58_out, or_59_out, or_60_out, or_62_out, or_64_out, or_66_out, or_68_out, or_69_out,
       or_71_out, or_72_out, or_74_out, or_77_out, or_79_out, stepper_1_step_2, stepper_1_step_3,
       stepper_1_step_4;
  wire [3:0] Y_OP_t;
  wire [4:0] ALU_Operation;
  wire [7:0] instruction_register_1_instruction_out;
  wire [15:0] multiplexer_1_out;

  not not_1 (not_1_out, EXT_INT);
  Multiplexer #(.enable("false"), .width(16)) multiplexer_1 (
    .in0(INSTRUCTION), .in1(16'h300), .out(multiplexer_1_out), .sel(EXT_INT));
  Instruction_Register instruction_register_1 (
    .ALU_OPERATION(ALU_Operation), .INSTRUCTION_OUT(instruction_register_1_instruction_out),
    .X_OPERAND(X_OP), .Y_OPERAND(Y_OP_t), .DATA_IN(multiplexer_1_out), .WE(STEP), .CLR(CLR));
  not not_2 (not_2_out, RESUME);
  not not_3 (not_3_out, Y_OP_t[2]);
  not not_4 (not_4_out, Y_OP_t[1]);
  not not_5 (not_5_out, Y_OP_t[0]);
  not not_6 (not_6_out, FLAGS_IN[0]);
  not not_7 (not_7_out, FLAGS_IN[1]);
  Instruction_Decoder instruction_decoder_1 (
    .MOV_FLAGS_REG(instruction_decoder_1_mov_flags_reg), .MOV_REG_REG(instruction_decoder_1_mov_reg_reg),
    .ALU_OPERATION(instruction_decoder_1_alu_operation), .BRK(instruction_decoder_1_brk),
    .ISR(instruction_decoder_1_isr), .HLT(instruction_decoder_1_hlt),
    .INT_DISABLE(instruction_decoder_1_int_disable), .INT_ENABLE(instruction_decoder_1_int_enable),
    .INT_CALL(instruction_decoder_1_int_call), .CALL_DIRECT(instruction_decoder_1_call_direct),
    .CALL_INDIRECT(instruction_decoder_1_call_indirect), .RET(instruction_decoder_1_ret),
    .RTI(instruction_decoder_1_rti), .LD_IMM(instruction_decoder_1_ld_imm), .LD(instruction_decoder_1_ld),
    .ST(instruction_decoder_1_st), .LD_ST_IMM_PTR(instruction_decoder_1_ld_st_imm_ptr),
    .LD_ST_INDIRECT(instruction_decoder_1_ld_st_indirect),
    .LD_ST_INDIRECT_OFFSET(instruction_decoder_1_ld_st_indirect_offset),
    .PUSH_REG(instruction_decoder_1_push_reg), .PUSH_FLAGS(instruction_decoder_1_push_flags),
    .POP_REG(instruction_decoder_1_pop_reg), .POP_FLAGS(instruction_decoder_1_pop_flags),
    .JMP_DIRECT(instruction_decoder_1_jmp_direct), .JMP_INDIRECT(instruction_decoder_1_jmp_indirect),
    .MOV_REG_FLAGS(instruction_decoder_1_mov_reg_flags), .Y_OPERAND(Y_OP_t),
    .INSTRUCTION_IN(instruction_register_1_instruction_out));  // open: TBI, CBI, SBI, IBI
  Stepper stepper_1 (
    .STEP_1(STEP), .STEP_2(stepper_1_step_2), .STEP_3(stepper_1_step_3), .STEP_4(stepper_1_step_4),
    .CLR(CLR), ._WE(or_6_out));  // open: RESET
  or or_1 (RAM_RE, or_7_out, and_14_out);
  and and_1 (and_1_out, not_5_out, not_4_out, not_3_out);
  and and_2 (and_2_out, FLAGS_IN[1], Y_OP_t[0], not_4_out, not_3_out);
  and and_3 (and_3_out, not_7_out, not_5_out, Y_OP_t[1], not_3_out);
  and and_4 (and_4_out, FLAGS_IN[0], Y_OP_t[0], Y_OP_t[1], not_3_out);
  and and_5 (and_5_out, not_6_out, not_5_out, not_4_out, Y_OP_t[2]);
  and and_6 (and_6_out, not_7_out, not_6_out);
  and and_7 (and_7_out, and_6_out, and_8_out);
  and and_8 (and_8_out, Y_OP_t[0], not_4_out, Y_OP_t[2]);
  or or_2 (or_2_out, FLAGS_IN[1], FLAGS_IN[0]);
  and and_9 (and_9_out, or_2_out, and_10_out);
  and and_10 (and_10_out, not_5_out, Y_OP_t[1], Y_OP_t[2]);
  or or_3 (PC_WE, or_13_out, or_14_out, or_15_out, or_16_out);
  or or_4 (PC_LOAD, or_17_out, or_18_out);
  or or_5 (GPR_WE, or_19_out, or_20_out);
  and and_11 (and_11_out, stepper_1_step_2, not_2_out, instruction_decoder_1_brk);
  and and_12 (and_12_out, stepper_1_step_2, instruction_decoder_1_hlt);
  or or_6 (or_6_out, and_11_out, and_12_out);
  or or_7 (or_7_out, or_25_out, or_26_out, or_27_out, or_28_out);
  or or_8 (RAM_WE, or_29_out, or_30_out, or_31_out);
  or or_9 (RAM_ADDR_MODE[1], or_32_out, or_33_out, or_34_out, or_35_out);
  or or_10 (or_10_out, and_1_out, and_2_out, and_3_out, and_4_out);
  or or_11 (or_11_out, or_10_out, or_12_out);
  or or_12 (or_12_out, and_5_out, and_7_out, and_9_out);
  or or_13 (or_13_out, and_23_out, and_24_out, and_25_out, and_27_out);
  or or_14 (or_14_out, and_17_out, ISS_WE, and_32_out, and_31_out);
  or or_15 (or_15_out, and_35_out, and_37_out, and_40_out);
  or or_16 (or_16_out, and_28_out, and_29_out, and_48_out, and_15_out);
  or or_17 (or_17_out, and_23_out, and_25_out, and_27_out);
  or or_18 (or_18_out, and_28_out, and_29_out, and_13_out);
  and and_13 (and_13_out, or_11_out, or_38_out);
  or or_19 (or_19_out, and_31_out, and_33_out, and_34_out, and_36_out);
  or or_20 (or_20_out, and_46_out, and_50_out, and_52_out, and_16_out);
  or or_21 (SP_INC, or_42_out, or_43_out);
  or or_22 (SP_DEC, or_44_out, or_45_out);
  or or_23 (INT_DISABLE, and_20_out, and_21_out);
  or or_24 (INT_ENABLE, and_19_out, and_29_out);
  or or_25 (or_25_out, and_17_out, ISS_WE, and_24_out, and_28_out);
  or or_26 (or_26_out, and_29_out, and_30_out, and_31_out, and_32_out);
  or or_27 (or_27_out, and_33_out, and_34_out, and_35_out, and_36_out);
  or or_28 (or_28_out, and_37_out, and_40_out, and_46_out, and_47_out);
  and and_14 (and_14_out, and_48_out, or_11_out);
  or or_29 (or_29_out, and_22_out, and_23_out, and_25_out);
  or or_30 (or_30_out, and_27_out, and_38_out, and_39_out);
  or or_31 (or_31_out, and_41_out, and_43_out, and_45_out);
  or or_32 (or_32_out, and_22_out, and_23_out, and_25_out, and_27_out);
  or or_33 (or_33_out, and_28_out, and_29_out, and_30_out);
  or or_34 (or_34_out, and_46_out, and_34_out, and_36_out, and_39_out);
  or or_35 (or_35_out, and_47_out, and_41_out, and_43_out, and_45_out);
  or or_36 (RAM_ADDR_MODE[0], and_33_out, and_36_out, and_38_out, and_41_out);
  or or_37 (PC_RE, and_23_out, and_25_out, and_27_out);
  and and_15 (and_15_out, or_11_out, and_49_out);
  or or_38 (or_38_out, and_48_out, and_49_out);
  or or_39 (RAM_ADDR_MODE_2[1], and_23_out, and_27_out, and_49_out);
  or or_40 (RAM_ADDR_MODE_2[0], and_23_out, and_25_out);
  or or_41 (GPR_RE, and_38_out, and_39_out, and_41_out, and_43_out);
  and and_16 (and_16_out, and_53_out, nand_1_out);
  or or_42 (or_42_out, and_28_out, and_29_out, and_30_out);
  or or_43 (or_43_out, and_46_out, and_47_out);
  or or_44 (or_44_out, and_21_out, and_22_out, and_24_out);
  or or_45 (or_45_out, and_26_out, and_42_out, and_44_out);
  or or_46 (GPR_ADDR_MODE[1], and_16_out, and_52_out);
  or or_47 (GPR_ADDR_MODE[0], and_50_out, and_52_out);
  and and_17 (and_17_out, STEP, not_1_out);
  and and_18 (ISS_WE, stepper_1_step_2, instruction_decoder_1_isr);
  and and_19 (and_19_out, stepper_1_step_2, instruction_decoder_1_int_enable);
  and and_20 (and_20_out, stepper_1_step_2, instruction_decoder_1_int_disable);
  and and_21 (and_21_out, stepper_1_step_2, instruction_decoder_1_int_call);
  and and_22 (and_22_out, stepper_1_step_3, instruction_decoder_1_int_call);
  and and_23 (and_23_out, stepper_1_step_4, instruction_decoder_1_int_call);
  and and_24 (and_24_out, stepper_1_step_2, instruction_decoder_1_call_direct);
  and and_25 (and_25_out, stepper_1_step_3, instruction_decoder_1_call_direct);
  and and_26 (and_26_out, stepper_1_step_2, instruction_decoder_1_call_indirect);
  and and_27 (and_27_out, stepper_1_step_3, instruction_decoder_1_call_indirect);
  and and_28 (and_28_out, stepper_1_step_2, instruction_decoder_1_ret);
  and and_29 (and_29_out, stepper_1_step_2, instruction_decoder_1_rti);
  and and_30 (and_30_out, stepper_1_step_3, instruction_decoder_1_rti);
  and and_31 (and_31_out, stepper_1_step_2, instruction_decoder_1_ld, instruction_decoder_1_ld_imm);
  and and_32 (and_32_out, stepper_1_step_2, instruction_decoder_1_ld_st_imm_ptr, instruction_decoder_1_ld);
  and and_33 (and_33_out, stepper_1_step_3, instruction_decoder_1_ld_st_imm_ptr, instruction_decoder_1_ld);
  and and_34 (and_34_out, stepper_1_step_2, instruction_decoder_1_ld_st_indirect, instruction_decoder_1_ld);
  and and_35 (and_35_out, stepper_1_step_2, instruction_decoder_1_ld_st_indirect_offset, instruction_decoder_1_ld);
  and and_36 (and_36_out, stepper_1_step_3, instruction_decoder_1_ld_st_indirect_offset, instruction_decoder_1_ld);
  and and_37 (and_37_out, stepper_1_step_2, instruction_decoder_1_ld_st_imm_ptr, instruction_decoder_1_st);
  and and_38 (and_38_out, stepper_1_step_3, instruction_decoder_1_ld_st_imm_ptr, instruction_decoder_1_st);
  and and_39 (and_39_out, stepper_1_step_2, instruction_decoder_1_ld_st_indirect, instruction_decoder_1_st);
  and and_40 (and_40_out, stepper_1_step_2, instruction_decoder_1_ld_st_indirect_offset, instruction_decoder_1_st);
  and and_41 (and_41_out, stepper_1_step_3, instruction_decoder_1_ld_st_indirect_offset, instruction_decoder_1_st);
  and and_42 (and_42_out, stepper_1_step_2, instruction_decoder_1_push_reg);
  and and_43 (and_43_out, stepper_1_step_3, instruction_decoder_1_push_reg);
  and and_44 (and_44_out, stepper_1_step_2, instruction_decoder_1_push_flags);
  and and_45 (and_45_out, stepper_1_step_3, instruction_decoder_1_push_flags);
  and and_46 (and_46_out, stepper_1_step_2, instruction_decoder_1_pop_reg);
  and and_47 (and_47_out, stepper_1_step_2, instruction_decoder_1_pop_flags);
  and and_48 (and_48_out, stepper_1_step_2, instruction_decoder_1_jmp_direct);
  and and_49 (and_49_out, stepper_1_step_2, instruction_decoder_1_jmp_indirect);
  and and_50 (and_50_out, stepper_1_step_2, instruction_decoder_1_mov_reg_flags);
  and and_51 (and_51_out, stepper_1_step_2, instruction_decoder_1_mov_flags_reg);
  and and_52 (and_52_out, stepper_1_step_2, instruction_decoder_1_mov_reg_reg);
  and and_53 (and_53_out, stepper_1_step_2, instruction_decoder_1_alu_operation);
  nand nand_1 (nand_1_out, ALU_Operation[4], ALU_Operation[3]);
  or or_48 (or_48_out, ISS_WE, and_24_out, and_32_out);
  or or_49 (or_49_out, and_35_out, and_37_out, and_40_out);
  or or_50 (FLAGS_RE, and_22_out, and_50_out, and_45_out);
  or or_51 (FLAGS_WE, and_30_out, and_47_out, and_51_out, and_53_out);
  or or_52 (FLAGS_LOAD, and_30_out, and_47_out, and_51_out);
  or or_53 (FLAGS_LOAD_BUS, and_30_out, and_47_out);
  or or_54 (or_54_out, and_22_out, and_23_out, and_25_out, and_27_out);
  or or_55 (or_55_out, and_28_out, and_29_out, and_30_out);
  or or_56 (or_56_out, and_43_out, and_45_out, and_46_out, and_47_out);
  or or_57 (IMM_WE, or_48_out, or_49_out);
  or or_58 (or_58_out, or_54_out, or_55_out, or_56_out);
  Multiplexer #(.enable("false"), .width(4)) multiplexer_2 (.in0(Y_OP_t), .in1(4'b1111), .out(Y_OP), .sel(or_58_out));
  Demultiplexer #(.enable("false"), .select(5)) demultiplexer_1 (
    .out0(demultiplexer_1_out0), .out1(demultiplexer_1_out1), .out2(demultiplexer_1_out2), .out3(ALU_ABS),
    .out4(demultiplexer_1_out4), .out5(demultiplexer_1_out5), .out6(demultiplexer_1_out6), .out7(ALU_NEG),
    .out8(demultiplexer_1_out8), .out9(demultiplexer_1_out9), .out10(demultiplexer_1_out10),
    .out11(demultiplexer_1_out11), .out12(demultiplexer_1_out12), .out13(demultiplexer_1_out13),
    .out14(demultiplexer_1_out14), .out15(demultiplexer_1_out15), .out16(demultiplexer_1_out16),
    .out17(demultiplexer_1_out17), .out18(demultiplexer_1_out18), .out19(demultiplexer_1_out19),
    .out20(demultiplexer_1_out20), .out21(ALU_OR), .out22(ALU_XOR), .out23(ALU_NOT),
    .out24(demultiplexer_1_out24), .out25(ALU_I_FLAGS), .out26(demultiplexer_1_out26),
    .out27(ALU_X_PASSTHROUGH), .in(and_53_out), .sel(ALU_Operation));  // open: out28, out29, out30, out31
  or or_59 (or_59_out, demultiplexer_1_out0, demultiplexer_1_out1, demultiplexer_1_out2);
  or or_60 (or_60_out, ALU_ABS, demultiplexer_1_out4, demultiplexer_1_out5, demultiplexer_1_out6);
  or or_61 (ALU_ADD, or_59_out, or_60_out, or_62_out);
  or or_62 (or_62_out, ALU_NEG, demultiplexer_1_out24, ALU_I_FLAGS);
  or or_63 (ALU_CARRY, demultiplexer_1_out1, demultiplexer_1_out5);
  or or_64 (or_64_out, demultiplexer_1_out4, demultiplexer_1_out5, demultiplexer_1_out6);
  or or_65 (ALU_SUB, or_64_out, or_66_out);
  or or_66 (or_66_out, demultiplexer_1_out24, ALU_I_FLAGS);
  or or_67 (ALU_INC, demultiplexer_1_out2, demultiplexer_1_out6);
  or or_68 (or_68_out, demultiplexer_1_out8, demultiplexer_1_out9, demultiplexer_1_out10, demultiplexer_1_out11);
  or or_69 (or_69_out, demultiplexer_1_out12, demultiplexer_1_out13, demultiplexer_1_out14, demultiplexer_1_out15);
  or or_70 (ALU_SHIFT, or_68_out, or_69_out, or_71_out);
  or or_71 (or_71_out, demultiplexer_1_out16, demultiplexer_1_out17, demultiplexer_1_out18, demultiplexer_1_out19);
  or or_72 (or_72_out, demultiplexer_1_out8, demultiplexer_1_out9, demultiplexer_1_out10);
  or or_73 (ALU_SHIFT_LEFT, or_72_out, or_74_out);
  or or_74 (or_74_out, demultiplexer_1_out11, demultiplexer_1_out16, demultiplexer_1_out17);
  or or_75 (ALU_SHIFT_A, demultiplexer_1_out10, demultiplexer_1_out11, demultiplexer_1_out14, demultiplexer_1_out15);
  or or_76 (ALU_ROTATE, demultiplexer_1_out16, demultiplexer_1_out17, demultiplexer_1_out18, demultiplexer_1_out19);
  or or_77 (or_77_out, demultiplexer_1_out9, demultiplexer_1_out11, demultiplexer_1_out13);
  or or_78 (ALU_Y_EMBEDED, or_77_out, or_79_out);
  or or_79 (or_79_out, demultiplexer_1_out15, demultiplexer_1_out17, demultiplexer_1_out19);
  or or_80 (ALU_AND, demultiplexer_1_out20, demultiplexer_1_out26);

  // Other names for the same wires on the sheet: Y_OPERAND[3:0] = Y_OP_t

  // Notes on the sheet:
  //   Jump Control Logic
  //   Immediate Register
  //   RAM Addressing Mode Logic
  //   PC Read Logic
  //   PC Write Logic
  //   PC Load Logic
  //   PC Addressing Mode
  //   GPR Read Logic
  //   GPR Write Logic
  //   Stack Pointer Logic
  //   GPR Addressing Mode
  //   Internal Signals
  //   Interrupt Control Logic
  //   RAM Read Logic
  //   RAM Write Logic
  //   Register File
  //   IMM Write Logic
  //   Flags Read Logic
  //   Flags Write Logic
  //   Flags Load Logic
  //   Y Operand Addressing Mode
  //   ALU Operations Logic
endmodule

module Stepper (
  input  RESET,
  input  CLR,
  input  _WE,
  output STEP_1,
  output STEP_2,
  output STEP_3,
  output STEP_4
);

  wire and_1_out, and_2_out, and_3_out, and_4_out, and_5_out, and_6_out, and_8_out, and_10_out, and_12_out,
       clock_1_out, d_ff_1_q, d_ff_2_q, d_ff_3_q, d_ff_4_q, multiplexer_1_out, multiplexer_2_out,
       multiplexer_3_out, multiplexer_4_out, nor_1_out, not_1_out, or_1_out, or_2_out, or_3_out, or_4_out,
       or_5_out;

  or or_1 (or_1_out, nor_1_out, or_3_out, RESET);
  or or_2 (or_2_out, and_1_out, and_2_out, and_3_out);
  or or_3 (or_3_out, or_2_out, or_4_out);
  or or_4 (or_4_out, and_4_out, and_5_out, and_6_out);
  or or_5 (or_5_out, or_1_out, d_ff_4_q);
  and and_1 (and_1_out, d_ff_4_q, d_ff_3_q);
  and and_2 (and_2_out, d_ff_4_q, d_ff_2_q);
  and and_3 (and_3_out, d_ff_3_q, d_ff_2_q);
  and and_4 (and_4_out, d_ff_4_q, d_ff_1_q);
  and and_5 (and_5_out, d_ff_3_q, d_ff_1_q);
  and and_6 (and_6_out, d_ff_2_q, d_ff_1_q);
  nor nor_1 (nor_1_out, d_ff_4_q, d_ff_3_q, d_ff_2_q, d_ff_1_q);
  D_Flip_Flop d_ff_1 (.D(multiplexer_1_out), .clk(clock_1_out), .Q(d_ff_1_q), .reset(CLR));  // open: Qn, preset
  Multiplexer #(.enable("false")) multiplexer_1 (.in0(or_5_out), .in1(d_ff_1_q), .out(multiplexer_1_out), .sel(_WE));
  not not_1 (not_1_out, or_1_out);
  and and_7 (STEP_1, d_ff_1_q, ~d_ff_2_q, ~d_ff_3_q, ~d_ff_4_q);  // AND_Gate
  and and_8 (and_8_out, d_ff_1_q, not_1_out);
  D_Flip_Flop d_ff_2 (.D(multiplexer_2_out), .clk(clock_1_out), .Q(d_ff_2_q), .reset(CLR));  // open: Qn, preset
  Multiplexer #(.enable("false")) multiplexer_2 (.in0(and_8_out), .in1(d_ff_2_q), .out(multiplexer_2_out), .sel(_WE));
  and and_9 (STEP_2, ~d_ff_1_q, d_ff_2_q, ~d_ff_3_q, ~d_ff_4_q);  // AND_Gate
  and and_10 (and_10_out, d_ff_2_q, not_1_out);
  D_Flip_Flop d_ff_3 (.D(multiplexer_3_out), .clk(clock_1_out), .Q(d_ff_3_q), .reset(CLR));  // open: Qn, preset
  Multiplexer #(.enable("false")) multiplexer_3 (.in0(and_10_out), .in1(d_ff_3_q), .out(multiplexer_3_out), .sel(_WE));
  and and_11 (STEP_3, ~d_ff_1_q, ~d_ff_2_q, d_ff_3_q, ~d_ff_4_q);  // AND_Gate
  and and_12 (and_12_out, d_ff_3_q, not_1_out);
  Multiplexer #(.enable("false")) multiplexer_4 (.in0(and_12_out), .in1(d_ff_4_q), .out(multiplexer_4_out), .sel(_WE));
  Clock clock_1 (.out(clock_1_out));
  and and_13 (STEP_4, ~d_ff_1_q, ~d_ff_2_q, ~d_ff_3_q, d_ff_4_q);  // AND_Gate
  D_Flip_Flop d_ff_4 (.D(multiplexer_4_out), .clk(clock_1_out), .Q(d_ff_4_q), .reset(CLR));  // open: Qn, preset
endmodule

module Instruction_Decoder (
  input  [3:0] Y_OPERAND,
  input  [7:0] INSTRUCTION_IN,
  output ISR,
  output INT_DISABLE,
  output INT_ENABLE,
  output INT_CALL,
  output CALL_DIRECT,
  output CALL_INDIRECT,
  output RET,
  output RTI,
  output LD_IMM,
  output LD,
  output ST,
  output LD_ST_IMM_PTR,
  output LD_ST_INDIRECT,
  output LD_ST_INDIRECT_OFFSET,
  output PUSH_REG,
  output PUSH_FLAGS,
  output POP_REG,
  output POP_FLAGS,
  output JMP_DIRECT,
  output JMP_INDIRECT,
  output MOV_REG_FLAGS,
  output MOV_FLAGS_REG,
  output MOV_REG_REG,
  output TBI,
  output CBI,
  output SBI,
  output IBI,
  output ALU_OPERATION,
  output BRK,
  output HLT
);

  wire and_3_out, and_7_out, and_10_out, and_13_out, and_14_out, and_15_out, and_16_out, and_17_out,
       and_18_out, and_20_out, and_23_out, decoder_1_out0, decoder_1_out7, decoder_2_out1, decoder_2_out2,
       decoder_2_out3, decoder_2_out4, decoder_2_out5, decoder_2_out8, decoder_2_out9, decoder_2_out10,
       decoder_2_out11, decoder_2_out13, decoder_2_out14, decoder_2_out15, decoder_2_out16, decoder_2_out17,
       decoder_2_out18, decoder_2_out19, decoder_2_out20, decoder_2_out21, decoder_2_out22, decoder_2_out23,
       decoder_2_out24, decoder_2_out25, decoder_2_out26, decoder_2_out30, decoder_2_out31, decoder_3_out0,
       decoder_3_out1;

  Decoder #(.enable("false"), .select(3)) decoder_1 (
    .out0(decoder_1_out0), .out1(ALU_OPERATION), .out7(decoder_1_out7), .sel(INSTRUCTION_IN[7:5]));  // open: out2, out3, out4, out5, out6
  Decoder #(.enable("false"), .select(5)) decoder_2 (
    .out1(decoder_2_out1), .out2(decoder_2_out2), .out3(decoder_2_out3), .out4(decoder_2_out4),
    .out5(decoder_2_out5), .out8(decoder_2_out8), .out9(decoder_2_out9), .out10(decoder_2_out10),
    .out11(decoder_2_out11), .out13(decoder_2_out13), .out14(decoder_2_out14), .out15(decoder_2_out15),
    .out16(decoder_2_out16), .out17(decoder_2_out17), .out18(decoder_2_out18), .out19(decoder_2_out19),
    .out20(decoder_2_out20), .out21(decoder_2_out21), .out22(decoder_2_out22), .out23(decoder_2_out23),
    .out24(decoder_2_out24), .out25(decoder_2_out25), .out26(decoder_2_out26), .out30(decoder_2_out30),
    .out31(decoder_2_out31), .sel(INSTRUCTION_IN[4:0]));  // open: out0, out6, out7, out12, out27, out28, out29
  Decoder #(.enable("false")) decoder_3 (.out0(decoder_3_out0), .out1(decoder_3_out1), .sel(Y_OPERAND[0]));
  and and_1 (ISR, decoder_2_out1, decoder_1_out0);
  and and_2 (INT_DISABLE, decoder_3_out0, and_3_out);
  and and_3 (and_3_out, decoder_2_out2, decoder_1_out0);
  and and_4 (INT_ENABLE, and_3_out, decoder_3_out1);
  and and_5 (INT_CALL, decoder_2_out3, decoder_1_out0);
  and and_6 (CALL_DIRECT, decoder_3_out0, and_7_out);
  and and_7 (and_7_out, decoder_2_out4, decoder_1_out0);
  and and_8 (CALL_INDIRECT, and_7_out, decoder_3_out1);
  and and_9 (RET, decoder_3_out0, and_10_out);
  and and_10 (and_10_out, decoder_2_out5, decoder_1_out0);
  and and_11 (RTI, and_10_out, decoder_3_out1);
  and and_12 (LD_IMM, decoder_2_out8, decoder_1_out0);
  and and_13 (and_13_out, decoder_2_out9, decoder_1_out0);
  and and_14 (and_14_out, decoder_2_out10, decoder_1_out0);
  and and_15 (and_15_out, decoder_2_out11, decoder_1_out0);
  and and_16 (and_16_out, decoder_2_out13, decoder_1_out0);
  and and_17 (and_17_out, decoder_2_out14, decoder_1_out0);
  and and_18 (and_18_out, decoder_2_out15, decoder_1_out0);
  and and_19 (PUSH_REG, decoder_3_out0, and_20_out);
  and and_20 (and_20_out, decoder_2_out16, decoder_1_out0);
  and and_21 (PUSH_FLAGS, and_20_out, decoder_3_out1);
  and and_22 (POP_REG, decoder_3_out0, and_23_out);
  and and_23 (and_23_out, decoder_2_out17, decoder_1_out0);
  and and_24 (POP_FLAGS, and_23_out, decoder_3_out1);
  and and_25 (JMP_DIRECT, decoder_2_out18, decoder_1_out0);
  and and_26 (JMP_INDIRECT, decoder_2_out19, decoder_1_out0);
  and and_27 (MOV_REG_FLAGS, decoder_2_out20, decoder_1_out0);
  and and_28 (MOV_FLAGS_REG, decoder_2_out21, decoder_1_out0);
  and and_29 (MOV_REG_REG, decoder_2_out22, decoder_1_out0);
  and and_30 (TBI, decoder_2_out23, decoder_1_out0);
  and and_31 (CBI, decoder_2_out24, decoder_1_out0);
  and and_32 (SBI, decoder_2_out25, decoder_1_out0);
  and and_33 (IBI, decoder_2_out26, decoder_1_out0);
  and and_34 (BRK, decoder_2_out30, decoder_1_out7);
  and and_35 (HLT, decoder_2_out31, decoder_1_out7);
  or or_1 (LD, LD_IMM, and_13_out, and_14_out, and_15_out);
  or or_2 (ST, and_16_out, and_17_out, and_18_out);
  or or_3 (LD_ST_IMM_PTR, and_13_out, and_16_out);
  or or_4 (LD_ST_INDIRECT, and_14_out, and_17_out);
  or or_5 (LD_ST_INDIRECT_OFFSET, and_15_out, and_18_out);
endmodule

module Program_Counter (
  input  [15:0] DATA_IN,
  input  WE,
  input  LOAD,
  input  CLR,
  input  RE,
  output [15:0] ADDR_OUT,
  output [15:0] DATA_OUT
);

  wire clock_1_out;
  wire [15:0] adder_1_out, bit_extender_1_out, multiplexer_1_out;

  Adder #(.width(16)) adder_1 (.a(ADDR_OUT), .b(16'h1), .out(adder_1_out), .cin(1'b0));  // open: cout
  Multiplexer #(.enable("false"), .width(16)) multiplexer_1 (
    .in0(adder_1_out), .in1(DATA_IN), .out(multiplexer_1_out), .sel(LOAD));
  Register #(.width(16)) PC (.D(multiplexer_1_out), .en(WE), .clk(clock_1_out), .Q(ADDR_OUT), .clr(CLR));
  Clock clock_1 (.out(clock_1_out));
  assign bit_extender_1_out = {{15{RE}}, RE};  // Bit_Extender bit_extender_1
  assign DATA_OUT = ADDR_OUT & bit_extender_1_out;  // AND_Gate and_1, 16 bits wide
endmodule

module Interrupt_Service_System (
  input  [15:0] DATA_IN,
  input  WE,
  input  INT_IN,
  input  ENABLE,
  input  DISABLE,
  input  CLR,
  output [15:0] DATA_OUT,
  output INT_OUT
);

  wire clock_1_out, ENABLED_q, or_1_out, TRIGGERED_q;

  Register #(.width(16)) ISR (.D(DATA_IN), .en(WE), .clk(clock_1_out), .Q(DATA_OUT), .clr(CLR));
  Clock clock_1 (.out(clock_1_out));
  D_Flip_Flop TRIGGERED (.D(INT_IN), .clk(clock_1_out), .Q(TRIGGERED_q), .reset(CLR));  // open: Qn, preset
  Register #(.width(1)) ENABLED (.D(ENABLE), .en(or_1_out), .clk(clock_1_out), .Q(ENABLED_q), .clr(CLR));
  or or_1 (or_1_out, ENABLE, DISABLE);
  and and_1 (INT_OUT, TRIGGERED_q, ENABLED_q);
endmodule

module Register_File (
  input  [15:0] DATA_IN,
  input  WE,
  input  [3:0] XOP,
  input  [3:0] YOP,
  input  SP_INC,
  input  SP_DEC,
  input  CLR,
  input  RE,
  output [15:0] Y_OUT,
  output [15:0] X_OUT,
  output [15:0] DATA_OUT
);

  wire clock_1_out, demultiplexer_1_out0, demultiplexer_1_out1, demultiplexer_1_out2, demultiplexer_1_out3,
       demultiplexer_1_out4, demultiplexer_1_out5, demultiplexer_1_out6, demultiplexer_1_out7,
       demultiplexer_1_out8, demultiplexer_1_out9, demultiplexer_1_out10, demultiplexer_1_out11,
       demultiplexer_1_out12, demultiplexer_1_out13, demultiplexer_1_out14, demultiplexer_1_out15, or_1_out,
       or_2_out;
  wire [15:0] adder_1_out, bit_extender_1_out, bit_extender_2_out, multiplexer_1_out, r0_q, r1_q, r2_q, r3_q,
       r4_q, r5_q, r6_q, r7_q, r8_q, r9_q, r10_q, r11_q, r12_q, r13_q, r14_q, r15_q;

  Demultiplexer #(.enable("false"), .select(4)) demultiplexer_1 (
    .out0(demultiplexer_1_out0), .out1(demultiplexer_1_out1), .out2(demultiplexer_1_out2),
    .out3(demultiplexer_1_out3), .out4(demultiplexer_1_out4), .out5(demultiplexer_1_out5),
    .out6(demultiplexer_1_out6), .out7(demultiplexer_1_out7), .out8(demultiplexer_1_out8),
    .out9(demultiplexer_1_out9), .out10(demultiplexer_1_out10), .out11(demultiplexer_1_out11),
    .out12(demultiplexer_1_out12), .out13(demultiplexer_1_out13), .out14(demultiplexer_1_out14),
    .out15(demultiplexer_1_out15), .in(WE), .sel(XOP));
  assign bit_extender_1_out = {{15{SP_DEC}}, SP_DEC};  // Bit_Extender bit_extender_1
  Adder #(.width(16)) adder_1 (.a(r15_q), .b(bit_extender_1_out), .out(adder_1_out), .cin(SP_INC));  // open: cout
  or or_1 (or_1_out, SP_INC, SP_DEC);
  Multiplexer #(.enable("false"), .width(16)) multiplexer_1 (
    .in0(DATA_IN), .in1(adder_1_out), .out(multiplexer_1_out), .sel(or_1_out));
  or or_2 (or_2_out, demultiplexer_1_out15, SP_INC, SP_DEC);
  Clock clock_1 (.out(clock_1_out));
  Register #(.width(16)) r0 (.D(DATA_IN), .en(demultiplexer_1_out0), .clk(clock_1_out), .Q(r0_q), .clr(CLR));
  Register #(.width(16)) r1 (.D(DATA_IN), .en(demultiplexer_1_out1), .clk(clock_1_out), .Q(r1_q), .clr(CLR));
  Register #(.width(16)) r2 (.D(DATA_IN), .en(demultiplexer_1_out2), .clk(clock_1_out), .Q(r2_q), .clr(CLR));
  Register #(.width(16)) r3 (.D(DATA_IN), .en(demultiplexer_1_out3), .clk(clock_1_out), .Q(r3_q), .clr(CLR));
  Register #(.width(16)) r4 (.D(DATA_IN), .en(demultiplexer_1_out4), .clk(clock_1_out), .Q(r4_q), .clr(CLR));
  Register #(.width(16)) r5 (.D(DATA_IN), .en(demultiplexer_1_out5), .clk(clock_1_out), .Q(r5_q), .clr(CLR));
  Register #(.width(16)) r6 (.D(DATA_IN), .en(demultiplexer_1_out6), .clk(clock_1_out), .Q(r6_q), .clr(CLR));
  Register #(.width(16)) r7 (.D(DATA_IN), .en(demultiplexer_1_out7), .clk(clock_1_out), .Q(r7_q), .clr(CLR));
  Register #(.width(16)) r8 (.D(DATA_IN), .en(demultiplexer_1_out8), .clk(clock_1_out), .Q(r8_q), .clr(CLR));
  Register #(.width(16)) r9 (.D(DATA_IN), .en(demultiplexer_1_out9), .clk(clock_1_out), .Q(r9_q), .clr(CLR));
  Register #(.width(16)) r10 (.D(DATA_IN), .en(demultiplexer_1_out10), .clk(clock_1_out), .Q(r10_q), .clr(CLR));
  Register #(.width(16)) r11 (.D(DATA_IN), .en(demultiplexer_1_out11), .clk(clock_1_out), .Q(r11_q), .clr(CLR));
  Register #(.width(16)) r12 (.D(DATA_IN), .en(demultiplexer_1_out12), .clk(clock_1_out), .Q(r12_q), .clr(CLR));
  Register #(.width(16)) r13 (.D(DATA_IN), .en(demultiplexer_1_out13), .clk(clock_1_out), .Q(r13_q), .clr(CLR));
  Register #(.width(16)) r14 (.D(DATA_IN), .en(demultiplexer_1_out14), .clk(clock_1_out), .Q(r14_q), .clr(CLR));
  Register #(.width(16)) r15 (.D(multiplexer_1_out), .en(or_2_out), .clk(clock_1_out), .Q(r15_q), .clr(CLR));
  Multiplexer #(.enable("false"), .select(4), .width(16)) multiplexer_2 (
    .in0(r0_q), .in1(r1_q), .in2(r2_q), .in3(r3_q), .in4(r4_q), .in5(r5_q), .in6(r6_q), .in7(r7_q),
    .in8(r8_q), .in9(r9_q), .in10(r10_q), .in11(r11_q), .in12(r12_q), .in13(r13_q), .in14(r14_q),
    .in15(r15_q), .out(Y_OUT), .sel(YOP));
  Multiplexer #(.enable("false"), .select(4), .width(16)) multiplexer_3 (
    .in0(r0_q), .in1(r1_q), .in2(r2_q), .in3(r3_q), .in4(r4_q), .in5(r5_q), .in6(r6_q), .in7(r7_q),
    .in8(r8_q), .in9(r9_q), .in10(r10_q), .in11(r11_q), .in12(r12_q), .in13(r13_q), .in14(r14_q),
    .in15(r15_q), .out(X_OUT), .sel(XOP));
  assign bit_extender_2_out = {{15{RE}}, RE};  // Bit_Extender bit_extender_2
  assign DATA_OUT = bit_extender_2_out & X_OUT;  // AND_Gate and_1, 16 bits wide

  // Notes on the sheet:
  //   Stack Pointer
endmodule

module Arithmetic_Logic_Unit (
  input  [1:0] FLAGS_READ,
  input  CARRY,
  input  SUB,
  input  NEG,
  input  ABS,
  input  INC,
  input  [15:0] A_OPERAND,
  input  [15:0] B_OPERAND,
  input  I_FLAGS,
  input  ADD,
  input  SHIFT,
  input  LEFT,
  input  ROTATE,
  input  A_SHIFT,
  input  AND,
  input  OR,
  input  XOR,
  input  NOT,
  input  X_PASS_THROUGH,
  output [15:0] RESULT,
  output [1:0] FLAGS_WRITE
);

  wire adder_1_cout, and_1_out, and_2_out, and_3_out, and_4_out, and_10_out, and_12_out, not_2_out, or_1_out,
       or_3_out, or_4_out, or_7_out, or_8_out, or_9_out, or_10_out, xor_2_out, xor_4_out;
  wire [3:0] bit_extender_8_out;
  wire [15:0] adder_1_out, and_5_out, and_6_out, and_7_out, and_8_out, and_9_out, and_11_out, and_13_out,
       bit_extender_1_out, bit_extender_2_out, bit_extender_3_out, bit_extender_4_out, bit_extender_5_out,
       bit_extender_6_out, bit_extender_7_out, bit_extender_9_out, multiplexer_1_out, multiplexer_2_out,
       multiplexer_3_out, multiplexer_4_out, multiplexer_5_out, multiplexer_6_out, not_1_out, or_2_out,
       or_5_out, shifter_1_out, shifter_2_out, shifter_3_out, xor_1_out, xor_3_out;

  assign bit_extender_1_out = {{15{AND}}, AND};  // Bit_Extender bit_extender_1
  assign bit_extender_2_out = {{15{OR}}, OR};  // Bit_Extender bit_extender_2
  assign bit_extender_3_out = {{15{XOR}}, XOR};  // Bit_Extender bit_extender_3
  assign bit_extender_4_out = {{15{NOT}}, NOT};  // Bit_Extender bit_extender_4
  assign bit_extender_5_out = {{15{X_PASS_THROUGH}}, X_PASS_THROUGH};  // Bit_Extender bit_extender_5
  and and_1 (and_1_out, FLAGS_READ[0], CARRY);
  and and_2 (and_2_out, ABS, A_OPERAND[15]);
  or or_1 (or_1_out, NEG, ABS);
  and and_3 (and_3_out, A_OPERAND[15], ~B_OPERAND[15]);  // AND_Gate
  and and_4 (and_4_out, B_OPERAND[15], ~A_OPERAND[15]);  // AND_Gate
  assign and_5_out = A_OPERAND & bit_extender_1_out & B_OPERAND;  // AND_Gate and_5, 16 bits wide
  assign and_6_out = bit_extender_2_out & or_2_out;  // AND_Gate and_6, 16 bits wide
  assign or_2_out = A_OPERAND | B_OPERAND;  // OR_Gate or_2, 16 bits wide
  assign and_7_out = bit_extender_3_out & xor_1_out;  // AND_Gate and_7, 16 bits wide
  assign xor_1_out = A_OPERAND ^ B_OPERAND;  // XOR_Gate xor_1, 16 bits wide
  assign and_8_out = bit_extender_4_out & not_1_out;  // AND_Gate and_8, 16 bits wide
  assign not_1_out = ~B_OPERAND;  // NOT_Gate not_1, 16 bits wide
  assign and_9_out = A_OPERAND & bit_extender_5_out;  // AND_Gate and_9, 16 bits wide
  or or_3 (or_3_out, SUB, NEG, and_2_out);
  Multiplexer #(.enable("false"), .width(16)) multiplexer_1 (
    .in0(B_OPERAND), .in1(16'h1), .out(multiplexer_1_out), .sel(INC));
  Multiplexer #(.enable("false"), .width(16)) multiplexer_2 (
    .in0(multiplexer_1_out), .in1(A_OPERAND), .out(multiplexer_2_out), .sel(or_1_out));
  or or_4 (or_4_out, and_3_out, and_4_out);
  assign or_5_out = and_5_out | and_6_out | and_7_out | and_8_out;  // OR_Gate or_5, 16 bits wide
  xor xor_2 (xor_2_out, and_1_out, or_3_out);
  assign bit_extender_6_out = {{15{not_2_out}}, not_2_out};  // Bit_Extender bit_extender_6
  not not_2 (not_2_out, or_1_out);
  assign bit_extender_7_out = {{15{or_3_out}}, or_3_out};  // Bit_Extender bit_extender_7
  and and_10 (and_10_out, or_4_out, I_FLAGS, ADD);
  Multiplexer #(.enable("false"), .width(16)) multiplexer_3 (
    .in0(A_OPERAND),
    .in1({A_OPERAND[0], A_OPERAND[1], A_OPERAND[2], A_OPERAND[3], A_OPERAND[4], A_OPERAND[5], A_OPERAND[6], A_OPERAND[7], A_OPERAND[8], A_OPERAND[9], A_OPERAND[10], A_OPERAND[11], A_OPERAND[12], A_OPERAND[13], A_OPERAND[14], A_OPERAND[15]}),
    .out(multiplexer_3_out), .sel(LEFT));
  Bit_Extender #(.in_width(16), .out_width(4), .\type ("zero")) bit_extender_8 (
    .in(B_OPERAND), .out(bit_extender_8_out));
  assign and_11_out = bit_extender_6_out & A_OPERAND;  // AND_Gate and_11, 16 bits wide
  assign xor_3_out = bit_extender_7_out ^ multiplexer_2_out;  // XOR_Gate xor_3, 16 bits wide
  Shifter #(.shift("lr"), .width(16)) shifter_1 (
    .in(multiplexer_3_out), .\dist (bit_extender_8_out), .out(shifter_1_out));
  Multiplexer #(.enable("false"), .width(16)) multiplexer_4 (
    .in0(shifter_1_out), .in1(shifter_2_out), .out(multiplexer_4_out), .sel(A_SHIFT));
  Shifter #(.shift("ar"), .width(16)) shifter_2 (
    .in(multiplexer_3_out), .\dist (bit_extender_8_out), .out(shifter_2_out));
  Shifter #(.shift("rr"), .width(16)) shifter_3 (
    .in(multiplexer_3_out), .\dist (bit_extender_8_out), .out(shifter_3_out));
  Adder #(.width(16)) adder_1 (.a(and_11_out), .b(xor_3_out), .out(adder_1_out), .cin(xor_2_out), .cout(adder_1_cout));
  xor xor_4 (xor_4_out, adder_1_cout, or_3_out);
  Multiplexer #(.enable("false"), .width(16)) multiplexer_5 (
    .in0(multiplexer_4_out), .in1(shifter_3_out), .out(multiplexer_5_out), .sel(ROTATE));
  assign bit_extender_9_out = {{15{ADD}}, ADD};  // Bit_Extender bit_extender_9
  and and_12 (and_12_out, xor_4_out, ADD);
  assign and_13_out = adder_1_out & bit_extender_9_out;  // AND_Gate and_13, 16 bits wide
  xor xor_5 (FLAGS_WRITE[0], and_12_out, and_10_out);
  Multiplexer #(.width(16)) multiplexer_6 (
    .in0(multiplexer_5_out),
    .in1({multiplexer_5_out[0], multiplexer_5_out[1], multiplexer_5_out[2], multiplexer_5_out[3], multiplexer_5_out[4], multiplexer_5_out[5], multiplexer_5_out[6], multiplexer_5_out[7], multiplexer_5_out[8], multiplexer_5_out[9], multiplexer_5_out[10], multiplexer_5_out[11], multiplexer_5_out[12], multiplexer_5_out[13], multiplexer_5_out[14], multiplexer_5_out[15]}),
    .out(multiplexer_6_out), .sel(LEFT), .en(SHIFT));
  assign RESULT = and_13_out | multiplexer_6_out | or_5_out | and_9_out;  // OR_Gate or_6, 16 bits wide
  or or_7 (or_7_out, RESULT[15], RESULT[14], RESULT[13], RESULT[12]);
  or or_8 (or_8_out, RESULT[11], RESULT[10], RESULT[9], RESULT[8]);
  nor nor_1 (FLAGS_WRITE[1], or_7_out, or_8_out, or_9_out, or_10_out);
  or or_9 (or_9_out, RESULT[7], RESULT[6], RESULT[5], RESULT[4]);
  or or_10 (or_10_out, RESULT[3], RESULT[2], RESULT[1], RESULT[0]);
endmodule

module Flags_Register (
  input  [1:0] ALU_OUT,
  input  [15:0] DATA_IN,
  input  LOAD,
  input  WE,
  input  CLR,
  input  RE,
  output [1:0] ALU_IN,
  output [15:0] DATA_OUT
);

  wire clock_1_out;
  wire [1:0] multiplexer_1_out;
  wire [15:0] bit_extender_1_out;

  Clock clock_1 (.out(clock_1_out));
  Multiplexer #(.enable("false"), .width(2)) multiplexer_1 (
    .in0(ALU_OUT), .in1(DATA_IN[1:0]), .out(multiplexer_1_out), .sel(LOAD));
  Register #(.width(2)) flags (.D(multiplexer_1_out), .en(WE), .clk(clock_1_out), .Q(ALU_IN), .clr(CLR));
  assign bit_extender_1_out = {{15{RE}}, RE};  // Bit_Extender bit_extender_1
  assign DATA_OUT = {{14{1'b0}}, ALU_IN} & bit_extender_1_out;  // AND_Gate and_1, 16 bits wide
endmodule

module Immediate_Register (
  input  [15:0] DATA_IN,
  input  WE,
  input  CLR,
  output [15:0] DATA_OUT
);

  wire clock_1_out;

  Register #(.width(16)) IMM (.D(DATA_IN), .en(WE), .clk(clock_1_out), .Q(DATA_OUT), .clr(CLR));
  Clock clock_1 (.out(clock_1_out));
endmodule
